# Fritzing sketch 28BYJ-48 stepper motor control with temperature sensor (saved by Fritzing 0.9.3b)
breadboards: 1

parts:
  LM35 = LM35 Temperature Sensor [package="TO92 [THT]"]
  part = Arduino Uno (Rev3)
  Stepper_motor = 28BYJ-48 Stepper Motor [part_number=28BYJ-48]
  part_2 = 28BYJ-48 Driver Module [part_number=ULN2003 package=THT]
  part_3 = Resistor [tolerance=±5% resistance=220 package="0402 [SMD]"]

nets:
  N1: LM35.+Vs, part_3.Pin_0
  N2: LM35.Vout, part.A1
  GND: LM35.GND, part.GND, part_2.GND
  N3: part.D8, part_2.IN1
  N4: part.D9_PWM, part_2.IN2
  N5: part.D10_PWM/SS, part_2.IN3
  N6: part.D11_PWM/MOSI, part_2.IN4
  N7: part.5V, part_3.Pin_1
  N8: Stepper_motor.blue-pin, part_2.blue-pin
  N9: Stepper_motor.pink-pin, part_2.pink-pin
  N10: Stepper_motor.yellow-pin, part_2.yellow-pin
  N11: Stepper_motor.orange-pin, part_2.orange-pin
  N12: Stepper_motor.red-pin, part_2.red-pin

custom parts:
  28BYJ-48 Stepper Motor: Unipolar Stepper Motor 28BYJ-48 Top coil - pink & orange Bottom coil - blue & yellow Common rail - red Connector pins: blue - pink - yellow - orange - red
  28BYJ-48 Driver Module: Generic male header
